# Fritzing sketch Schematics (saved by Fritzing 0.9.3b)
breadboards: 1

parts:
  Raspberry_Pi_1 = Raspberry Pi 3 [part_number=RPI-3-V1.2]
  PWM1 = PCA9685 16x12-bit PWM Breakout
  IC1 = Rasberry Pi NIOR Camera [chip_label=IC package="DIP (Dual Inline) [THT]"]  # not connected
  J1 = Basic Servo
  J7 = Basic Servo
  J8 = Basic Servo
  J9 = Basic Servo
  J10 = Basic Servo
  J11 = Basic Servo
  VCC1 = Battery block 9V  # not connected

nets:
  N1: Raspberry_Pi_1.GPIO2, PWM1.no_name_yet#504
  N2: Raspberry_Pi_1.GPIO3, PWM1.no_name_yet#503
  N3: Raspberry_Pi_1.GND, PWM1.no_name_yet#501, PWM1.no_name_yet#601, PWM1.no_name_yet#1000, PWM1.no_name_yet#1001, PWM1.no_name_yet#1002, PWM1.no_name_yet#1003, PWM1.no_name_yet#1004, PWM1.no_name_yet#1005
  N4: Raspberry_Pi_1.5V, PWM1.no_name_yet#505
  N5: PWM1.no_name_yet#0, J1.pulse
  N6: PWM1.no_name_yet#1, J7.pulse
  N7: PWM1.no_name_yet#2, J8.pulse
  N8: PWM1.no_name_yet#3, J9.pulse
  N9: PWM1.no_name_yet#4, J10.pulse
  N10: PWM1.no_name_yet#5, J11.pulse
  N11: PWM1.no_name_yet#100, PWM1.no_name_yet#101, PWM1.no_name_yet#102, PWM1.no_name_yet#103, PWM1.no_name_yet#104, PWM1.no_name_yet#105, PWM1.no_name_yet#606

custom parts:
  Rasberry Pi NIOR Camera: Camera
